// Logisim project semprojcpu.circ as structural Verilog: 12 circuits, main circuit main
module ALU8 (
  input  [3:0] aluop,
  input  [7:0] a,
  input  [7:0] b,
  output zero,
  output [7:0] result,
  output overflow
);

  wire alu1_1_c_out, alu1_2_c_out, alu1_3_c_out, alu1_4_c_out, alu1_5_c_out, alu1_6_c_out, alu1_7_c_out,
       alumsb_1_set, or_1_out;

  alu1 alu1_1 (
    .A(aluop[3]), .B(b[0]), .out(result[0]), .b_invert(aluop[2]), .C_in(aluop[2]), .op(aluop[1:0]),
    .C_out(alu1_1_c_out), .a_invert(a[0]), .less(alumsb_1_set));
  alu1 alu1_2 (
    .A(aluop[3]), .B(b[1]), .out(result[1]), .b_invert(aluop[2]), .C_in(alu1_1_c_out), .op(aluop[1:0]),
    .C_out(alu1_2_c_out), .a_invert(a[1]), .less(1'b0));
  alu1 alu1_3 (
    .A(aluop[3]), .B(b[2]), .out(result[2]), .b_invert(aluop[2]), .C_in(alu1_2_c_out), .op(aluop[1:0]),
    .C_out(alu1_3_c_out), .a_invert(a[2]), .less(1'b0));
  alu1 alu1_4 (
    .A(aluop[3]), .B(b[3]), .out(result[3]), .b_invert(aluop[2]), .C_in(alu1_3_c_out), .op(aluop[1:0]),
    .C_out(alu1_4_c_out), .a_invert(a[3]), .less(1'b0));
  alu1 alu1_5 (
    .A(aluop[3]), .B(b[4]), .out(result[4]), .b_invert(aluop[2]), .C_in(alu1_4_c_out), .op(aluop[1:0]),
    .C_out(alu1_5_c_out), .a_invert(a[4]), .less(1'b0));
  alu1 alu1_6 (
    .A(aluop[3]), .B(b[5]), .out(result[5]), .b_invert(aluop[2]), .C_in(alu1_5_c_out), .op(aluop[1:0]),
    .C_out(alu1_6_c_out), .a_invert(a[5]), .less(1'b0));
  alu1 alu1_7 (
    .A(aluop[3]), .B(b[6]), .out(result[6]), .b_invert(aluop[2]), .C_in(alu1_6_c_out), .op(aluop[1:0]),
    .C_out(alu1_7_c_out), .a_invert(a[6]), .less(1'b0));
  aluMSB alumsb_1 (
    .A(a[7]), .B(b[7]), .less(1'b0), .out(result[7]), .set(alumsb_1_set), .oflow(overflow),
    .a_invert(aluop[3]), .b_invert(aluop[2]), .C_in(alu1_7_c_out), .op(aluop[1:0]));
  or or_1 (or_1_out, result[0], result[1], result[2], result[3], result[4], result[5], result[6], result[7]);
  not not_1 (zero, or_1_out);
endmodule

module main (
  input  on
);

  wire alu16_1_zero, and_1_out, CLK, control_1_alusrc, control_1_branch, control_1_jump, control_1_memread,
       control_1_memwrite, control_1_regwrite, not_1_out, RST;
  wire [1:0] control_1_aluop, control_1_memtoreg, control_1_regdst;
  wire [3:0] alucontrol_1_out_3, multiplexer_1_out;
  wire [15:0] adder_1_out, adder_2_out, alu16_1_result, bit_extender_1_out, multiplexer_2_out,
       multiplexer_3_out, multiplexer_4_out, multiplexer_5_out, PC_q, ram_1_data, regfile_1_regdata1,
       regfile_1_regdata2, shifter_1_out;
  wire [18:0] rom_1_data;

  Register #(.width(16)) PC (.D(multiplexer_4_out), .en(on), .Q(PC_q), .clk(CLK), .clr(RST));
  Button RESET (.out(RST));
  Clock clock_1 (.out(CLK));
  Adder #(.width(16)) adder_1 (.a(16'h1), .b(PC_q), .out(adder_1_out));  // open: cin, cout
  ROM #(.addrWidth(16), .dataWidth(19)) rom_1 (.addr(PC_q), .data(rom_1_data));  // open: sel
  Multiplexer #(.select(2), .width(4), .enable("false")) multiplexer_1 (
    .in0(rom_1_data[11:8]), .in1(rom_1_data[7:4]), .in2(4'b1111), .out(multiplexer_1_out),
    .sel(control_1_regdst));  // open: in3
  RegFile regfile_1 (
    .RegRead1(rom_1_data[15:12]), .RegRead2(rom_1_data[11:8]), .RegWrite_2(multiplexer_1_out),
    .DIn(multiplexer_5_out), .RegData1(regfile_1_regdata1), .RegData2(regfile_1_regdata2),
    .RegWrite(control_1_regwrite), .CLK(CLK), .Reset(RST));
  assign bit_extender_1_out = {{8{rom_1_data[7]}}, rom_1_data[7:0]};  // Bit_Extender bit_extender_1
  control control_1 (
    .RegDst(control_1_regdst), .Branch(control_1_branch), .Jump(control_1_jump), .ALUOp(control_1_aluop),
    .MemtoReg(control_1_memtoreg), .OP(rom_1_data[18:16]), .MemRead(control_1_memread),
    .MemWrite(control_1_memwrite), .ALUSrc(control_1_alusrc), .RegWrite(control_1_regwrite));
  Shifter #(.width(16)) shifter_1 (.in(bit_extender_1_out), .\dist (4'b0000), .out(shifter_1_out));
  Multiplexer #(.width(16), .enable("false")) multiplexer_2 (
    .in0(regfile_1_regdata2), .in1(bit_extender_1_out), .out(multiplexer_2_out), .sel(control_1_alusrc));
  alucontrol alucontrol_1 (.ALUOp(control_1_aluop), .Func(rom_1_data[3:0]), .out_3(alucontrol_1_out_3));
  and and_1 (and_1_out, control_1_branch, alu16_1_zero);
  Adder #(.width(16)) adder_2 (.a(adder_1_out), .b(shifter_1_out), .out(adder_2_out));  // open: cin, cout
  ALU16 alu16_1 (
    .aluop(alucontrol_1_out_3), .in_2(regfile_1_regdata1), .in_3(multiplexer_2_out), .zero(alu16_1_zero),
    .result(alu16_1_result));  // open: oflow
  Multiplexer #(.width(16), .enable("false")) multiplexer_3 (
    .in0(adder_1_out), .in1(adder_2_out), .out(multiplexer_3_out), .sel(and_1_out));
  Multiplexer #(.width(16), .enable("false")) multiplexer_4 (
    .in0(multiplexer_3_out), .in1(rom_1_data[15:0]), .out(multiplexer_4_out), .sel(control_1_jump));
  not not_1 (not_1_out, CLK);
  RAM #(.addrWidth(16), .dataWidth(16), .bus("separate")) ram_1 (
    .addr(alu16_1_result), .din(regfile_1_regdata2), .data(ram_1_data), .str(control_1_memwrite),
    .clk(not_1_out), .ld(control_1_memread), .clr(RST));  // open: sel
  Multiplexer #(.select(2), .width(16), .enable("false")) multiplexer_5 (
    .in0(alu16_1_result), .in1(ram_1_data), .in2(adder_1_out), .out(multiplexer_5_out),
    .sel(control_1_memtoreg));  // open: in3

  // Notes on the sheet:
  //   contents of rom_1 (hex, n*v repeats v):
  //   30701 30801 5d700 5d801
endmodule

module adder1bit (
  input  C_in,
  input  A,
  input  B,
  output S,
  output C_out
);

  wire and_1_out, and_2_out, xor_1_out;

  xor xor_1 (xor_1_out, A, B);
  and and_1 (and_1_out, A, B);
  xor xor_2 (S, xor_1_out, C_in);
  and and_2 (and_2_out, xor_1_out, C_in);
  or or_1 (C_out, and_2_out, and_1_out);
endmodule

module alu1 (
  input  a_invert,
  input  b_invert,
  input  [1:0] op,
  input  C_in,
  input  A,
  input  B,
  input  less,
  output out,
  output C_out
);

  wire add_out, adder1bit_1_s, and_1_out, and_2_out, and_3_out, and_4_out, and_5_out, and_6_out, less_out,
       not_1_out, not_2_out, not_3_out, not_4_out, not_5_out, not_6_out, or_1_out, or_2_out, or_3_out,
       or_4_out;

  not not_1 (not_1_out, a_invert);
  not not_2 (not_2_out, A);
  not not_3 (not_3_out, B);
  not not_4 (not_4_out, b_invert);
  and and_1 (and_1_out, A, not_1_out);
  and and_2 (and_2_out, a_invert, not_2_out);
  and and_3 (and_3_out, not_4_out, B);
  or or_1 (or_1_out, and_3_out, and_4_out);
  and and_4 (and_4_out, b_invert, not_3_out);
  and and_5 (and_5_out, or_2_out, or_1_out);
  or or_2 (or_2_out, and_1_out, and_2_out);
  or or_3 (or_3_out, or_2_out, or_1_out);
  adder1bit adder1bit_1 (.A(or_2_out), .B(or_1_out), .S(adder1bit_1_s), .C_in(C_in), .C_out(C_out));
  not not_5 (not_5_out, op[1]);
  not not_6 (not_6_out, op[0]);
  and and_6 (and_6_out, not_6_out, not_5_out, and_5_out);
  and or_4 (or_4_out, op[0], or_3_out, not_5_out);
  and add (add_out, not_6_out, adder1bit_1_s, op[1]);
  and u_less (less_out, op[0], less, op[1]);
  or or_5 (out, and_6_out, or_4_out, add_out, less_out);
endmodule

module aluMSB (
  input  [1:0] op,
  input  a_invert,
  input  b_invert,
  input  C_in,
  input  A,
  input  B,
  input  less,
  output out,
  output set,
  output oflow
);

  wire add_out, adder1bit_1_c_out, and_1_out, and_2_out, and_3_out, and_4_out, and_5_out, and_6_out,
       less_out, not_1_out, not_2_out, not_3_out, not_4_out, not_5_out, not_6_out, or_1_out, or_2_out,
       or_3_out, or_4_out;

  not not_1 (not_1_out, b_invert);
  not not_2 (not_2_out, a_invert);
  not not_3 (not_3_out, A);
  not not_4 (not_4_out, B);
  and and_1 (and_1_out, A, not_2_out);
  or or_1 (or_1_out, and_1_out, and_2_out);
  and and_2 (and_2_out, a_invert, not_3_out);
  and and_3 (and_3_out, not_1_out, B);
  or or_2 (or_2_out, and_3_out, and_4_out);
  and and_4 (and_4_out, b_invert, not_4_out);
  aluOflow aluoflow_1 (.b_inv(b_invert), .a(or_1_out), .b(or_2_out), .c_in(adder1bit_1_c_out), .s(set), .out_6(oflow));
  and and_5 (and_5_out, or_1_out, or_2_out);
  or or_3 (or_3_out, or_1_out, or_2_out);
  adder1bit adder1bit_1 (.A(or_1_out), .B(or_2_out), .S(set), .C_in(C_in), .C_out(adder1bit_1_c_out));
  not not_5 (not_5_out, op[1]);
  not not_6 (not_6_out, op[0]);
  and and_6 (and_6_out, not_6_out, not_5_out, and_5_out);
  and or_4 (or_4_out, op[0], or_3_out, not_5_out);
  and add (add_out, not_6_out, set, op[1]);
  and u_less (less_out, op[0], less, op[1]);
  or or_5 (out, and_6_out, or_4_out, add_out, less_out);
endmodule

module aluOflow (
  input  b_inv,
  input  a,
  input  b,
  input  c_in,
  input  s,
  output out_6
);

  wire xnor_1_out, xor_1_out;

  xnor xnor_1 (xnor_1_out, a, b);
  and and_1 (out_6, xnor_1_out, xor_1_out);
  xor xor_1 (xor_1_out, c_in, s);
endmodule

module ALU16 (
  input  [3:0] aluop,
  input  [15:0] in_2,
  input  [15:0] in_3,
  output zero,
  output [15:0] result,
  output oflow
);

  wire alu1_1_c_out, alu1_2_c_out, alu1_3_c_out, alu1_4_c_out, alu1_5_c_out, alu1_6_c_out, alu1_7_c_out,
       alu1_8_c_out, alu1_9_c_out, alu1_10_c_out, alu1_11_c_out, alu1_12_c_out, alu1_13_c_out, alu1_14_c_out,
       alu1_15_c_out, alumsb_1_set, or_1_out;

  alu1 alu1_1 (
    .A(aluop[3]), .B(in_3[0]), .out(result[0]), .b_invert(aluop[2]), .C_in(aluop[2]), .op(aluop[1:0]),
    .C_out(alu1_1_c_out), .a_invert(in_2[0]), .less(alumsb_1_set));
  alu1 alu1_2 (
    .A(aluop[3]), .B(in_3[1]), .out(result[1]), .b_invert(aluop[2]), .C_in(alu1_1_c_out), .op(aluop[1:0]),
    .C_out(alu1_2_c_out), .a_invert(in_2[1]), .less(1'b0));
  alu1 alu1_3 (
    .A(aluop[3]), .B(in_3[2]), .out(result[2]), .b_invert(aluop[2]), .C_in(alu1_2_c_out), .op(aluop[1:0]),
    .C_out(alu1_3_c_out), .a_invert(in_2[2]), .less(1'b0));
  alu1 alu1_4 (
    .A(aluop[3]), .B(in_3[3]), .out(result[3]), .b_invert(aluop[2]), .C_in(alu1_3_c_out), .op(aluop[1:0]),
    .C_out(alu1_4_c_out), .a_invert(in_2[3]), .less(1'b0));
  alu1 alu1_5 (
    .A(aluop[3]), .B(in_3[4]), .out(result[4]), .b_invert(aluop[2]), .C_in(alu1_4_c_out), .op(aluop[1:0]),
    .C_out(alu1_5_c_out), .a_invert(in_2[4]), .less(1'b0));
  alu1 alu1_6 (
    .A(aluop[3]), .B(in_3[5]), .out(result[5]), .b_invert(aluop[2]), .C_in(alu1_5_c_out), .op(aluop[1:0]),
    .C_out(alu1_6_c_out), .a_invert(in_2[5]), .less(1'b0));
  alu1 alu1_7 (
    .A(aluop[3]), .B(in_3[6]), .out(result[6]), .b_invert(aluop[2]), .C_in(alu1_6_c_out), .op(aluop[1:0]),
    .C_out(alu1_7_c_out), .a_invert(in_2[6]), .less(1'b0));
  alu1 alu1_8 (
    .A(aluop[3]), .B(in_3[7]), .out(result[7]), .b_invert(aluop[2]), .C_in(alu1_7_c_out), .op(aluop[1:0]),
    .C_out(alu1_8_c_out), .a_invert(in_2[7]), .less(1'b0));
  alu1 alu1_9 (
    .A(aluop[3]), .B(in_3[8]), .out(result[8]), .b_invert(aluop[2]), .C_in(alu1_8_c_out), .op(aluop[1:0]),
    .C_out(alu1_9_c_out), .a_invert(in_2[8]), .less(1'b0));
  alu1 alu1_10 (
    .A(aluop[3]), .B(in_3[9]), .out(result[9]), .b_invert(aluop[2]), .C_in(alu1_9_c_out), .op(aluop[1:0]),
    .C_out(alu1_10_c_out), .a_invert(in_2[9]), .less(1'b0));
  alu1 alu1_11 (
    .A(aluop[3]), .B(in_3[10]), .out(result[10]), .b_invert(aluop[2]), .C_in(alu1_10_c_out), .op(aluop[1:0]),
    .C_out(alu1_11_c_out), .a_invert(in_2[10]), .less(1'b0));
  alu1 alu1_12 (
    .A(aluop[3]), .B(in_3[11]), .out(result[11]), .b_invert(aluop[2]), .C_in(alu1_11_c_out), .op(aluop[1:0]),
    .C_out(alu1_12_c_out), .a_invert(in_2[11]), .less(1'b0));
  alu1 alu1_13 (
    .A(aluop[3]), .B(in_3[12]), .out(result[12]), .b_invert(aluop[2]), .C_in(alu1_12_c_out), .op(aluop[1:0]),
    .C_out(alu1_13_c_out), .a_invert(in_2[12]), .less(1'b0));
  alu1 alu1_14 (
    .A(aluop[3]), .B(in_3[13]), .out(result[13]), .b_invert(aluop[2]), .C_in(alu1_13_c_out), .op(aluop[1:0]),
    .C_out(alu1_14_c_out), .a_invert(in_2[13]), .less(1'b0));
  alu1 alu1_15 (
    .A(aluop[3]), .B(in_3[14]), .out(result[14]), .b_invert(aluop[2]), .C_in(alu1_14_c_out), .op(aluop[1:0]),
    .C_out(alu1_15_c_out), .a_invert(in_2[14]), .less(1'b0));
  aluMSB alumsb_1 (
    .A(in_2[15]), .B(in_3[15]), .less(1'b0), .out(result[15]), .set(alumsb_1_set), .oflow(oflow),
    .a_invert(aluop[3]), .b_invert(aluop[2]), .C_in(alu1_15_c_out), .op(aluop[1:0]));
  or or_1 (or_1_out, result[8], result[9], result[10], result[11], result[12], result[13], result[14], result[15], result[0], result[1], result[2], result[3], result[4], result[5], result[6], result[7]);
  not not_1 (zero, or_1_out);
endmodule

module _3bitEquality (
  input  [2:0] in_1,
  input  [2:0] in_2,
  output out_3
);

  wire [2:0] xnor_1_out;

  assign xnor_1_out = ~(in_1 ^ in_2);  // XNOR_Gate xnor_1, 3 bits wide
  and and_1 (out_3, xnor_1_out[0], xnor_1_out[1], xnor_1_out[2]);
endmodule

module control (
  input  [2:0] OP,
  output [1:0] RegDst,
  output Branch,
  output Jump,
  output [1:0] ALUOp,
  output [1:0] MemtoReg,
  output MemRead,
  output MemWrite,
  output ALUSrc,
  output RegWrite
);

  wire n3bitequality_5_out_3, n3bitequality_7_out_3, or_1_out;
  wire [1:0] and_1_out, and_2_out, and_3_out, bit_extender_1_out, bit_extender_2_out, bit_extender_3_out;

  _3bitEquality u_3bitequality_1 (.in_1(3'b111), .in_2(OP));  // open: out_3
  _3bitEquality u_3bitequality_2 (.in_1(3'b110), .in_2(OP), .out_3(MemtoReg[1]));
  _3bitEquality u_3bitequality_3 (.in_1(3'b101), .in_2(OP), .out_3(MemWrite));
  _3bitEquality u_3bitequality_4 (.in_1(3'b100), .in_2(OP), .out_3(MemRead));
  _3bitEquality u_3bitequality_5 (.in_1(3'b011), .in_2(OP), .out_3(n3bitequality_5_out_3));
  _3bitEquality u_3bitequality_6 (.in_1(3'b010), .in_2(OP), .out_3(Branch));
  _3bitEquality u_3bitequality_7 (.in_1(3'b001), .in_2(OP), .out_3(n3bitequality_7_out_3));
  _3bitEquality u_3bitequality_8 (.in_1(3'b000), .in_2(OP), .out_3(RegDst[0]));
  or or_1 (or_1_out, MemRead, MemWrite, n3bitequality_5_out_3);
  assign bit_extender_1_out = {{1{Branch}}, Branch};  // Bit_Extender bit_extender_1
  assign bit_extender_2_out = {{1{or_1_out}}, or_1_out};  // Bit_Extender bit_extender_2
  assign bit_extender_3_out = {{1{RegDst[0]}}, RegDst[0]};  // Bit_Extender bit_extender_3
  or or_2 (Jump, n3bitequality_7_out_3, MemtoReg[1]);
  assign and_1_out = bit_extender_1_out & 2'b01;  // AND_Gate and_1, 2 bits wide
  assign and_2_out = bit_extender_2_out & 2'b00;  // AND_Gate and_2, 2 bits wide
  assign and_3_out = bit_extender_3_out & 2'b10;  // AND_Gate and_3, 2 bits wide
  or or_3 (ALUSrc, MemRead, MemWrite, n3bitequality_5_out_3);
  or or_4 (RegWrite, MemRead, n3bitequality_5_out_3, RegDst[0]);
  assign ALUOp = and_1_out | and_2_out | and_3_out;  // OR_Gate or_5, 2 bits wide

  assign MemtoReg[0] = MemRead;
  assign RegDst[1] = MemtoReg[1];

  // Notes on the sheet:
  //   sw
  //   lw
  //   addi
  //   beq
  //   R Type
  //   jr
  //   jal
  //   j
endmodule

module alucontrol (
  input  [1:0] ALUOp,
  input  [3:0] Func,
  output [3:0] out_3
);

  wire n2biteq_1_out_3, n2biteq_2_out_3, n2biteq_3_out_3;

  _2bitEq u_2biteq_1 (.in_1(ALUOp), .in_2(2'b00), .out_3(n2biteq_1_out_3));
  _2bitEq u_2biteq_2 (.in_1(ALUOp), .in_2(2'b01), .out_3(n2biteq_2_out_3));
  _2bitEq u_2biteq_3 (.in_1(ALUOp), .in_2(2'b10), .out_3(n2biteq_3_out_3));
  assign out_3 = n2biteq_1_out_3 ? 4'b0010 : 4'bz;  // Controlled_Buffer controlled_buffer_1
  assign out_3 = n2biteq_2_out_3 ? 4'b0110 : 4'bz;  // Controlled_Buffer controlled_buffer_2
  assign out_3 = n2biteq_3_out_3 ? Func : 4'bz;  // Controlled_Buffer controlled_buffer_3
endmodule

module _2bitEq (
  input  [1:0] in_1,
  input  [1:0] in_2,
  output out_3
);

  wire [1:0] xnor_1_out;

  assign xnor_1_out = ~(in_1 ^ in_2);  // XNOR_Gate xnor_1, 2 bits wide
  and and_1 (out_3, xnor_1_out[0], xnor_1_out[1]);
endmodule

module RegFile (
  input  RegWrite,
  input  [3:0] RegRead1,
  input  [3:0] RegRead2,
  input  [3:0] RegWrite_2,
  input  [15:0] DIn,
  input  CLK,
  input  Reset,
  output [15:0] RegData1,
  output [15:0] RegData2
);

  wire decoder_1_out0, decoder_1_out1, decoder_1_out2, decoder_1_out3, decoder_1_out4, decoder_1_out5,
       decoder_1_out6, decoder_1_out7, decoder_1_out8, decoder_1_out9, decoder_1_out10, decoder_1_out11,
       decoder_1_out12, decoder_1_out13, decoder_1_out14, decoder_1_out15;
  wire [15:0] register_1_q, register_2_q, register_3_q, register_4_q, register_5_q, register_6_q,
       register_7_q, register_8_q, register_9_q, register_10_q, register_11_q, register_12_q, register_13_q,
       register_14_q, register_15_q, register_16_q;

  Decoder #(.select(4), .disabled(0)) decoder_1 (
    .out0(decoder_1_out0), .out1(decoder_1_out1), .out2(decoder_1_out2), .out3(decoder_1_out3),
    .out4(decoder_1_out4), .out5(decoder_1_out5), .out6(decoder_1_out6), .out7(decoder_1_out7),
    .out8(decoder_1_out8), .out9(decoder_1_out9), .out10(decoder_1_out10), .out11(decoder_1_out11),
    .out12(decoder_1_out12), .out13(decoder_1_out13), .out14(decoder_1_out14), .out15(decoder_1_out15),
    .sel(RegWrite_2), .en(RegWrite));
  Register #(.width(16)) register_1 (.D(DIn), .en(decoder_1_out0), .Q(register_1_q), .clk(CLK), .clr(Reset));
  Register #(.width(16)) register_2 (.D(DIn), .en(decoder_1_out1), .Q(register_2_q), .clk(CLK), .clr(Reset));
  Register #(.width(16)) register_3 (.D(DIn), .en(decoder_1_out2), .Q(register_3_q), .clk(CLK), .clr(Reset));
  Register #(.width(16)) register_4 (.D(DIn), .en(decoder_1_out3), .Q(register_4_q), .clk(CLK), .clr(Reset));
  Register #(.width(16)) register_5 (.D(DIn), .en(decoder_1_out4), .Q(register_5_q), .clk(CLK), .clr(Reset));
  Register #(.width(16)) register_6 (.D(DIn), .en(decoder_1_out5), .Q(register_6_q), .clk(CLK), .clr(Reset));
  Register #(.width(16)) register_7 (.D(DIn), .en(decoder_1_out6), .Q(register_7_q), .clk(CLK), .clr(Reset));
  Register #(.width(16)) register_8 (.D(DIn), .en(decoder_1_out7), .Q(register_8_q), .clk(CLK), .clr(Reset));
  Register #(.width(16)) register_9 (.D(DIn), .en(decoder_1_out8), .Q(register_9_q), .clk(CLK), .clr(Reset));
  Register #(.width(16)) register_10 (.D(DIn), .en(decoder_1_out9), .Q(register_10_q), .clk(CLK), .clr(Reset));
  Register #(.width(16)) register_11 (.D(DIn), .en(decoder_1_out10), .Q(register_11_q), .clk(CLK), .clr(Reset));
  Register #(.width(16)) register_12 (.D(DIn), .en(decoder_1_out11), .Q(register_12_q), .clk(CLK), .clr(Reset));
  Register #(.width(16)) register_13 (.D(DIn), .en(decoder_1_out12), .Q(register_13_q), .clk(CLK), .clr(Reset));
  Register #(.width(16)) register_14 (.D(DIn), .en(decoder_1_out13), .Q(register_14_q), .clk(CLK), .clr(Reset));
  Register #(.width(16)) register_15 (.D(DIn), .en(decoder_1_out14), .Q(register_15_q), .clk(CLK), .clr(Reset));
  Register #(.width(16)) register_16 (.D(DIn), .en(decoder_1_out15), .Q(register_16_q), .clk(CLK), .clr(Reset));
  Multiplexer #(.select(4), .width(16), .enable("false")) multiplexer_1 (
    .in0(register_1_q), .in1(register_2_q), .in2(register_3_q), .in3(register_4_q), .in4(register_5_q),
    .in5(register_6_q), .in6(register_7_q), .in7(register_8_q), .in8(register_9_q), .in9(register_10_q),
    .in10(register_11_q), .in11(register_12_q), .in12(register_13_q), .in13(register_14_q),
    .in14(register_15_q), .in15(register_16_q), .out(RegData1), .sel(RegRead1));
  Multiplexer #(.select(4), .width(16), .enable("false")) multiplexer_2 (
    .in0(register_1_q), .in1(register_2_q), .in2(register_3_q), .in3(register_4_q), .in4(register_5_q),
    .in5(register_6_q), .in6(register_7_q), .in7(register_8_q), .in8(register_9_q), .in9(register_10_q),
    .in10(register_11_q), .in11(register_12_q), .in12(register_13_q), .in13(register_14_q),
    .in14(register_15_q), .in15(register_16_q), .out(RegData2), .sel(RegRead2));

  // Notes on the sheet:
  //   0: $0
endmodule
